// Logisim project CPU_but_how_do_it_know.circ as structural Verilog: 60 circuits, main circuit main
module main (
  input  in_1,
  input  in_2,
  input  in_3,
  input  in_4,
  input  in_5,
  input  in_6,
  input  MARs,
  input  RAMs,
  input  RAMe,
  input  [7:0] CPUbus_In,
  input  IAR_s,
  input  IR_s,
  input  in_13,
  input  in_14,
  output IOclke,
  output IOclks,
  output IorO,
  output DorA,
  output [7:0] CPUbus_Out
);

  wire alu_1_out_7, alu_1_out_8, alu_1_out_9, alu_1_out_11, controlunit3_1_acc_e, controlunit3_1_acc_s,
       controlunit3_1_alu1, controlunit3_1_alu2, controlunit3_1_alu3, controlunit3_1_bus1_e,
       controlunit3_1_flag_s, controlunit3_1_iar_e, controlunit3_1_iar_s, controlunit3_1_mar_s,
       controlunit3_1_ram_e, controlunit3_1_ram_s, controlunit3_1_tmp_s, flags_1_out_7, flags_1_out_8,
       flags_1_out_9, flags_1_out_10, or_1_out, or_2_out, or_3_out, or_4_out, or_5_out;
  wire [7:0] alu_1_out_10, bus1_1_out_3, tmp_1_out_3;

  bus1 bus1_1 (.in_1(tmp_1_out_3), .in_2(controlunit3_1_bus1_e), .out_3(bus1_1_out_3));
  ALU alu_1 (
    .in_1(CPUbus_Out), .in_2(bus1_1_out_3), .in_4(controlunit3_1_alu1), .in_5(controlunit3_1_alu2),
    .in_6(controlunit3_1_alu3), .in_3(flags_1_out_7), .out_7(alu_1_out_7), .out_8(alu_1_out_8),
    .out_11(alu_1_out_11), .out_10(alu_1_out_10), .out_9(alu_1_out_9));
  ACC acc_1 (.in_1(alu_1_out_10), .in_2(controlunit3_1_acc_s), .in_3(controlunit3_1_acc_e), .out_4(CPUbus_Out));
  TMP tmp_1 (.in_1(CPUbus_Out), .in_2(or_1_out), .out_3(tmp_1_out_3));
  or or_1 (or_1_out, in_5, controlunit3_1_tmp_s);
  Flags flags_1 (
    .in_2(alu_1_out_11), .in_3(alu_1_out_8), .in_4(alu_1_out_7), .in_5(alu_1_out_9), .in_1(in_6),
    .in_6(controlunit3_1_flag_s), .out_7(flags_1_out_7), .out_8(flags_1_out_8), .out_9(flags_1_out_9),
    .out_10(flags_1_out_10));
  or or_2 (or_2_out, IAR_s, controlunit3_1_iar_s);
  IAR iar_1 (.in_1(CPUbus_Out), .in_2(or_2_out), .in_3(controlunit3_1_iar_e), .out_4(CPUbus_Out));
  Controlunit3 controlunit3_1 (
    .carryout(flags_1_out_7), .alarger(flags_1_out_8), .equal(flags_1_out_9), .zero(flags_1_out_10),
    .in_7(CPUbus_Out), .in_2(in_6), .in_12(CPUbus_Out), .IRs(IR_s), .R3_s(in_4), .R2_s(in_3), .R1_s(in_2),
    .R0_s(in_1), .bus1_e(controlunit3_1_bus1_e), .IAR_e(controlunit3_1_iar_e), .RAM_e(controlunit3_1_ram_e),
    .ACC_e(controlunit3_1_acc_e), .IOclk_e(IOclke), .ALU1(controlunit3_1_alu1), .ALU2(controlunit3_1_alu2),
    .ALU3(controlunit3_1_alu3), .out_30(CPUbus_Out), .DorA(DorA), .IorO(IorO), .MAR_s(controlunit3_1_mar_s),
    .IAR_s(controlunit3_1_iar_s), .ACC_s(controlunit3_1_acc_s), .RAM_s(controlunit3_1_ram_s),
    .TMP_s(controlunit3_1_tmp_s), .Flag_s(controlunit3_1_flag_s), .IOclk_s(IOclks));
  or or_3 (or_3_out, MARs, controlunit3_1_mar_s);
  or or_4 (or_4_out, controlunit3_1_ram_s, RAMs);
  or or_5 (or_5_out, controlunit3_1_ram_e, RAMe);
  RAM256 ram256_1 (
    .in_3(CPUbus_Out), .in_2(or_3_out), .in_4(or_4_out), .in_5(or_5_out), .in_1(CPUbus_Out),
    .out_6(CPUbus_Out));
  registerBEsimple registerbesimple_1 (.in_1(CPUbus_In), .in_2(in_13), .in_3(in_14), .out_4(CPUbus_Out));
endmodule

module memorybit (
  input  in_1,
  input  in_2,
  output out_3
);

  wire nand_1_out, nand_2_out, nand_4_out;

  nand nand_1 (nand_1_out, in_1, in_2);
  nand nand_2 (nand_2_out, nand_1_out, in_2);
  nand nand_3 (out_3, nand_1_out, nand_4_out);
  nand nand_4 (nand_4_out, out_3, nand_2_out);
endmodule

module \byte  (
  input  in_1,
  input  in_2,
  input  in_3,
  input  in_4,
  input  in_5,
  input  in_6,
  input  in_7,
  input  in_8,
  input  in_9,
  output out_10,
  output out_11,
  output out_12,
  output out_13,
  output out_14,
  output out_15,
  output out_16,
  output out_17
);

  memorybit memorybit_1 (.in_2(in_9), .in_1(in_1), .out_3(out_10));
  memorybit memorybit_2 (.in_2(in_9), .in_1(in_2), .out_3(out_11));
  memorybit memorybit_3 (.in_2(in_9), .in_1(in_3), .out_3(out_12));
  memorybit memorybit_4 (.in_2(in_9), .in_1(in_4), .out_3(out_13));
  memorybit memorybit_5 (.in_2(in_9), .in_1(in_5), .out_3(out_14));
  memorybit memorybit_6 (.in_2(in_9), .in_1(in_6), .out_3(out_15));
  memorybit memorybit_7 (.in_2(in_9), .in_1(in_7), .out_3(out_16));
  memorybit memorybit_8 (.in_2(in_9), .in_1(in_8), .out_3(out_17));
endmodule

module enabler (
  input  in_1,
  input  in_2,
  input  in_3,
  input  in_4,
  input  in_5,
  input  in_6,
  input  in_7,
  input  in_8,
  input  in_9,
  output out_10,
  output out_11,
  output out_12,
  output out_13,
  output out_14,
  output out_15,
  output out_16,
  output out_17
);

  assign out_10 = in_9 ? in_1 : 1'bz;  // Controlled_Buffer controlled_buffer_1
  assign out_11 = in_9 ? in_2 : 1'bz;  // Controlled_Buffer controlled_buffer_2
  assign out_12 = in_9 ? in_3 : 1'bz;  // Controlled_Buffer controlled_buffer_3
  assign out_13 = in_9 ? in_4 : 1'bz;  // Controlled_Buffer controlled_buffer_4
  assign out_14 = in_9 ? in_5 : 1'bz;  // Controlled_Buffer controlled_buffer_5
  assign out_15 = in_9 ? in_6 : 1'bz;  // Controlled_Buffer controlled_buffer_6
  assign out_16 = in_9 ? in_7 : 1'bz;  // Controlled_Buffer controlled_buffer_7
  assign out_17 = in_9 ? in_8 : 1'bz;  // Controlled_Buffer controlled_buffer_8
endmodule

module registerBE (
  input  in_1,
  input  in_2,
  input  in_3,
  input  in_4,
  input  in_5,
  input  in_6,
  input  in_7,
  input  in_8,
  input  in_9,
  input  in_10,
  output out_11,
  output out_12,
  output out_13,
  output out_14,
  output out_15,
  output out_16,
  output out_17,
  output out_18
);

  wire byte_1_out_10, byte_1_out_11, byte_1_out_12, byte_1_out_13, byte_1_out_14, byte_1_out_15,
       byte_1_out_16, byte_1_out_17;

  \byte  byte_1 (
    .in_3(in_3), .in_4(in_4), .in_5(in_5), .in_6(in_6), .in_7(in_7), .in_8(in_8), .in_1(in_1), .in_2(in_2),
    .in_9(in_9), .out_12(byte_1_out_12), .out_13(byte_1_out_13), .out_14(byte_1_out_14),
    .out_15(byte_1_out_15), .out_16(byte_1_out_16), .out_17(byte_1_out_17), .out_10(byte_1_out_10),
    .out_11(byte_1_out_11));
  enabler enabler_1 (
    .in_1(byte_1_out_10), .in_2(byte_1_out_11), .in_3(byte_1_out_12), .in_4(byte_1_out_13),
    .in_5(byte_1_out_14), .in_6(byte_1_out_15), .in_7(byte_1_out_16), .in_8(byte_1_out_17), .in_9(in_10),
    .out_10(out_11), .out_11(out_12), .out_12(out_13), .out_13(out_14), .out_14(out_15), .out_15(out_16),
    .out_16(out_17), .out_17(out_18));
endmodule

module magicbus (
  input  [7:0] in_1,
  input  in_2,
  input  in_3,
  input  in_4,
  input  in_5,
  input  in_6,
  input  in_7,
  input  in_8,
  input  in_9,
  input  in_10,
  input  in_11,
  output [7:0] out_12
);

  registerBEsimple registerbesimple_1 (.in_1(in_1), .in_2(in_2), .in_3(in_3), .out_4(out_12));
  registerBEsimple registerbesimple_2 (.in_1(out_12), .in_2(in_4), .in_3(in_5), .out_4(out_12));
  registerBEsimple registerbesimple_3 (.in_1(out_12), .in_2(in_6), .in_3(in_7), .out_4(out_12));
  registerBEsimple registerbesimple_4 (.in_1(out_12), .in_2(in_8), .in_3(in_9), .out_4(out_12));
  registerBEsimple registerbesimple_5 (.in_1(out_12), .in_2(in_10), .in_3(in_11), .out_4(out_12));
endmodule

module registerBEsimple (
  input  [7:0] in_1,
  input  in_2,
  input  in_3,
  output [7:0] out_4
);

  registerBE registerbe_1 (
    .in_9(in_2), .in_10(in_3), .in_1(in_1[0]), .in_2(in_1[1]), .in_3(in_1[2]), .in_4(in_1[3]),
    .in_5(in_1[4]), .in_6(in_1[5]), .in_7(in_1[6]), .in_8(in_1[7]), .out_11(out_4[0]), .out_12(out_4[1]),
    .out_13(out_4[2]), .out_14(out_4[3]), .out_15(out_4[4]), .out_16(out_4[5]), .out_17(out_4[6]),
    .out_18(out_4[7]));
endmodule

module RAM256Cell (
  input  in_1,
  input  [7:0] in_2,
  input  in_3,
  input  in_4,
  input  in_5,
  output [7:0] out_6
);

  wire and_1_out, and_2_out, and_3_out;

  and and_1 (and_1_out, in_1, in_3);
  and and_2 (and_2_out, and_1_out, in_4);
  and and_3 (and_3_out, and_1_out, in_5);
  registerBEsimple registerbesimple_1 (.in_1(in_2), .in_2(and_2_out), .in_3(and_3_out), .out_4(out_6));
endmodule

module MUX2to1 (
  input  in_1,
  input  in_2,
  input  in_3,
  output out_4
);

  wire and_1_out, and_2_out, not_1_out;

  and and_1 (and_1_out, in_1, in_3);
  and and_2 (and_2_out, in_2, not_1_out);
  not not_1 (not_1_out, in_3);
  or or_1 (out_4, and_1_out, and_2_out);
endmodule

module MUX8bit2to1 (
  input  [7:0] in_1,
  input  [7:0] in_2,
  input  in_3,
  output [7:0] out_4
);

  MUX2to1 mux2to1_1 (.in_1(in_1[0]), .in_2(in_2[0]), .in_3(in_3), .out_4(out_4[0]));
  MUX2to1 mux2to1_2 (.in_1(in_1[1]), .in_2(in_2[1]), .in_3(in_3), .out_4(out_4[1]));
  MUX2to1 mux2to1_3 (.in_1(in_1[2]), .in_2(in_2[2]), .in_3(in_3), .out_4(out_4[2]));
  MUX2to1 mux2to1_4 (.in_1(in_1[3]), .in_2(in_2[3]), .in_3(in_3), .out_4(out_4[3]));
  MUX2to1 mux2to1_5 (.in_1(in_1[4]), .in_2(in_2[4]), .in_3(in_3), .out_4(out_4[4]));
  MUX2to1 mux2to1_6 (.in_1(in_1[5]), .in_2(in_2[5]), .in_3(in_3), .out_4(out_4[5]));
  MUX2to1 mux2to1_7 (.in_1(in_1[6]), .in_2(in_2[6]), .in_3(in_3), .out_4(out_4[6]));
  MUX2to1 mux2to1_8 (.in_1(in_1[7]), .in_2(in_2[7]), .in_3(in_3), .out_4(out_4[7]));
endmodule

module RAM4times4 (
  input  in_1,
  input  in_2,
  input  in_3,
  input  in_4,
  input  in_5,
  input  in_6,
  input  in_7,
  input  in_8,
  input  in_9,
  input  in_10,
  input  in_11,
  input  in_12,
  input  in_13,
  input  [7:0] in_14,
  input  in_15,
  input  in_16,
  input  in_17,
  output [7:0] out_18,
  output [7:0] out_19,
  output [7:0] out_20,
  output out_21
);

  wire [7:0] adder8bit_1_out_5, controlled_buffer_1_out, mux8bit2to1_1_out_4;

  RAM256Cell ram256cell_1 (.in_1(in_3), .in_3(in_1), .in_4(in_10), .in_5(in_11), .in_2(out_19), .out_6(out_19));
  RAM256Cell ram256cell_2 (.in_1(in_6), .in_3(in_1), .in_4(in_10), .in_5(in_11), .in_2(out_19), .out_6(out_19));
  RAM256Cell ram256cell_3 (.in_1(in_3), .in_3(in_2), .in_4(in_10), .in_5(in_11), .in_2(out_19), .out_6(out_19));
  RAM256Cell ram256cell_4 (.in_1(in_6), .in_3(in_2), .in_4(in_10), .in_5(in_11), .in_2(out_19), .out_6(out_19));
  assign controlled_buffer_1_out = in_12 ? mux8bit2to1_1_out_4 : 8'bz;  // Controlled_Buffer controlled_buffer_1
  MUX8bit2to1 mux8bit2to1_1 (.in_3(in_17), .in_1(out_19), .in_2(in_14), .out_4(mux8bit2to1_1_out_4));
  registerBEsimple registerbesimple_1 (.in_1(controlled_buffer_1_out), .in_2(in_12), .in_3(in_13), .out_4(out_19));
  registerBEsimple registerbesimple_2 (.in_1(out_19), .in_2(in_4), .in_3(in_5), .out_4(out_18));
  registerBEsimple registerbesimple_3 (.in_1(out_19), .in_2(in_7), .in_3(in_8), .out_4(out_20));
  registerBEsimple registerbesimple_4 (.in_1(adder8bit_1_out_5), .in_2(in_15), .in_3(in_16), .out_4(out_19));
  adder8bit adder8bit_1 (.in_2(in_9), .in_3(out_20), .in_1(out_18), .out_4(out_21), .out_5(adder8bit_1_out_5));
endmodule

module adderbit1 (
  input  in_1,
  input  in_2,
  output out_3,
  output out_4
);

  xor xor_1 (out_3, in_1, in_2);
  and and_1 (out_4, in_1, in_2);
endmodule

module adder3bit1 (
  input  in_1,
  input  in_2,
  input  in_3,
  output out_4,
  output out_5
);

  wire adderbit1_1_out_3, adderbit1_1_out_4, adderbit1_2_out_4;

  adderbit1 adderbit1_1 (.in_1(in_2), .in_2(in_3), .out_3(adderbit1_1_out_3), .out_4(adderbit1_1_out_4));
  adderbit1 adderbit1_2 (.in_1(in_1), .in_2(adderbit1_1_out_3), .out_3(out_4), .out_4(adderbit1_2_out_4));
  or or_1 (out_5, adderbit1_2_out_4, adderbit1_1_out_4);
endmodule

module adder8bit (
  input  [7:0] in_1,
  input  in_2,
  input  [7:0] in_3,
  output out_4,
  output [7:0] out_5
);

  wire adder3bit1_2_out_5, adder3bit1_3_out_5, adder3bit1_4_out_5, adder3bit1_5_out_5, adder3bit1_6_out_5,
       adder3bit1_7_out_5, adder3bit1_8_out_5;

  adder3bit1 adder3bit1_1 (.in_2(in_1[7]), .in_3(in_3[7]), .in_1(adder3bit1_2_out_5), .out_4(out_5[7]), .out_5(out_4));
  adder3bit1 adder3bit1_2 (
    .in_2(in_1[6]), .in_3(in_3[6]), .in_1(adder3bit1_3_out_5), .out_4(out_5[6]), .out_5(adder3bit1_2_out_5));
  adder3bit1 adder3bit1_3 (
    .in_2(in_1[5]), .in_3(in_3[5]), .in_1(adder3bit1_4_out_5), .out_4(out_5[5]), .out_5(adder3bit1_3_out_5));
  adder3bit1 adder3bit1_4 (
    .in_2(in_1[4]), .in_3(in_3[4]), .in_1(adder3bit1_5_out_5), .out_4(out_5[4]), .out_5(adder3bit1_4_out_5));
  adder3bit1 adder3bit1_5 (
    .in_2(in_1[3]), .in_3(in_3[3]), .in_1(adder3bit1_6_out_5), .out_4(out_5[3]), .out_5(adder3bit1_5_out_5));
  adder3bit1 adder3bit1_6 (
    .in_2(in_1[2]), .in_3(in_3[2]), .in_1(adder3bit1_7_out_5), .out_4(out_5[2]), .out_5(adder3bit1_6_out_5));
  adder3bit1 adder3bit1_7 (
    .in_2(in_1[1]), .in_3(in_3[1]), .in_1(adder3bit1_8_out_5), .out_4(out_5[1]), .out_5(adder3bit1_7_out_5));
  adder3bit1 adder3bit1_8 (.in_2(in_1[0]), .in_3(in_3[0]), .in_1(in_2), .out_4(out_5[0]), .out_5(adder3bit1_8_out_5));
endmodule

module leftshifters (
  input  in_1,
  input  [7:0] in_2,
  output [7:0] out_3,
  output out_4
);

  wire registerbe_1_out_11, registerbe_1_out_12, registerbe_1_out_13, registerbe_1_out_14,
       registerbe_1_out_15, registerbe_1_out_16, registerbe_1_out_17;

  registerBE registerbe_1 (
    .in_9(1'b1), .in_10(1'b1), .in_1(in_2[0]), .in_2(in_2[1]), .in_3(in_2[2]), .in_4(in_2[3]),
    .in_5(in_2[4]), .in_6(in_2[5]), .in_7(in_2[6]), .in_8(in_2[7]), .out_11(registerbe_1_out_11),
    .out_12(registerbe_1_out_12), .out_13(registerbe_1_out_13), .out_14(registerbe_1_out_14),
    .out_15(registerbe_1_out_15), .out_16(registerbe_1_out_16), .out_17(registerbe_1_out_17), .out_18(out_4));
  registerBE registerbe_2 (
    .in_9(1'b1), .in_10(1'b1), .in_1(in_1), .in_2(registerbe_1_out_11), .in_3(registerbe_1_out_12),
    .in_4(registerbe_1_out_13), .in_5(registerbe_1_out_14), .in_6(registerbe_1_out_15),
    .in_7(registerbe_1_out_16), .in_8(registerbe_1_out_17), .out_11(out_3[0]), .out_12(out_3[1]),
    .out_13(out_3[2]), .out_14(out_3[3]), .out_15(out_3[4]), .out_16(out_3[5]), .out_17(out_3[6]),
    .out_18(out_3[7]));
endmodule

module rightshifters (
  input  [7:0] in_1,
  input  in_2,
  output out_3,
  output [7:0] out_4
);

  wire registerbe_1_out_12, registerbe_1_out_13, registerbe_1_out_14, registerbe_1_out_15,
       registerbe_1_out_16, registerbe_1_out_17, registerbe_1_out_18;

  registerBE registerbe_1 (
    .in_9(1'b1), .in_10(1'b1), .in_1(in_1[0]), .in_2(in_1[1]), .in_3(in_1[2]), .in_4(in_1[3]),
    .in_5(in_1[4]), .in_6(in_1[5]), .in_7(in_1[6]), .in_8(in_1[7]), .out_11(out_3),
    .out_12(registerbe_1_out_12), .out_13(registerbe_1_out_13), .out_14(registerbe_1_out_14),
    .out_15(registerbe_1_out_15), .out_16(registerbe_1_out_16), .out_17(registerbe_1_out_17),
    .out_18(registerbe_1_out_18));
  registerBE registerbe_2 (
    .in_9(1'b1), .in_10(1'b1), .in_1(registerbe_1_out_12), .in_2(registerbe_1_out_13),
    .in_3(registerbe_1_out_14), .in_4(registerbe_1_out_15), .in_5(registerbe_1_out_16),
    .in_6(registerbe_1_out_17), .in_7(registerbe_1_out_18), .in_8(in_2), .out_11(out_4[0]),
    .out_12(out_4[1]), .out_13(out_4[2]), .out_14(out_4[3]), .out_15(out_4[4]), .out_16(out_4[5]),
    .out_17(out_4[6]), .out_18(out_4[7]));
endmodule

module NoTter (
  input  [7:0] in_1,
  output [7:0] out_2
);

  not not_1 (out_2[0], in_1[0]);
  not not_2 (out_2[1], in_1[1]);
  not not_3 (out_2[2], in_1[2]);
  not not_4 (out_2[3], in_1[3]);
  not not_5 (out_2[4], in_1[4]);
  not not_6 (out_2[5], in_1[5]);
  not not_7 (out_2[6], in_1[6]);
  not not_8 (out_2[7], in_1[7]);
endmodule

module ANDer (
  input  [7:0] in_1,
  input  [7:0] in_2,
  output [7:0] out_3
);

  and and_1 (out_3[0], in_1[0], in_2[0]);
  and and_2 (out_3[1], in_1[1], in_2[1]);
  and and_3 (out_3[2], in_1[2], in_2[2]);
  and and_4 (out_3[3], in_1[3], in_2[3]);
  and and_5 (out_3[4], in_1[4], in_2[4]);
  and and_6 (out_3[5], in_1[5], in_2[5]);
  and and_7 (out_3[6], in_1[6], in_2[6]);
  and and_8 (out_3[7], in_1[7], in_2[7]);
endmodule

module ORer (
  input  [7:0] in_1,
  input  [7:0] in_2,
  output [7:0] out_3
);

  or or_1 (out_3[0], in_1[0], in_2[0]);
  or or_2 (out_3[1], in_1[1], in_2[1]);
  or or_3 (out_3[2], in_1[2], in_2[2]);
  or or_4 (out_3[3], in_1[3], in_2[3]);
  or or_5 (out_3[4], in_1[4], in_2[4]);
  or or_6 (out_3[5], in_1[5], in_2[5]);
  or or_7 (out_3[6], in_1[6], in_2[6]);
  or or_8 (out_3[7], in_1[7], in_2[7]);
endmodule

module XORer (
  input  [7:0] in_1,
  input  [7:0] in_2,
  output [7:0] out_3
);

  xor xor_1 (out_3[0], in_1[0], in_2[0]);
  xor xor_2 (out_3[1], in_1[1], in_2[1]);
  xor xor_3 (out_3[2], in_1[2], in_2[2]);
  xor xor_4 (out_3[3], in_1[3], in_2[3]);
  xor xor_5 (out_3[4], in_1[4], in_2[4]);
  xor xor_6 (out_3[5], in_1[5], in_2[5]);
  xor xor_7 (out_3[6], in_1[6], in_2[6]);
  xor xor_8 (out_3[7], in_1[7], in_2[7]);
endmodule

module Zero (
  input  [7:0] in_1,
  output out_2
);

  wire or_1_out;

  or or_1 (or_1_out, in_1[0], in_1[1], in_1[2], in_1[3], in_1[4], in_1[5], in_1[6], in_1[7]);
  not not_1 (out_2, or_1_out);
endmodule

module Comparator8bit (
  input  [7:0] in_1,
  input  [7:0] in_2,
  output [7:0] out_3,
  output out_4,
  output out_5
);

  wire comparator1bit_1_out_6, comparator1bit_1_out_7, comparator1bit_2_out_6, comparator1bit_2_out_7,
       comparator1bit_3_out_6, comparator1bit_3_out_7, comparator1bit_4_out_6, comparator1bit_4_out_7,
       comparator1bit_5_out_6, comparator1bit_5_out_7, comparator1bit_6_out_6, comparator1bit_6_out_7,
       comparator1bit_7_out_6, comparator1bit_7_out_7;

  Comparator1bit comparator1bit_1 (
    .in_3(in_1[7]), .in_4(in_2[7]), .in_1(1'b1), .in_2(1'b0), .out_6(comparator1bit_1_out_6),
    .out_7(comparator1bit_1_out_7), .out_5(out_3[7]));
  Comparator1bit comparator1bit_2 (
    .in_3(in_1[6]), .in_4(in_2[6]), .in_1(comparator1bit_1_out_6), .in_2(comparator1bit_1_out_7),
    .out_6(comparator1bit_2_out_6), .out_7(comparator1bit_2_out_7), .out_5(out_3[6]));
  Comparator1bit comparator1bit_3 (
    .in_3(in_1[5]), .in_4(in_2[5]), .in_1(comparator1bit_2_out_6), .in_2(comparator1bit_2_out_7),
    .out_6(comparator1bit_3_out_6), .out_7(comparator1bit_3_out_7), .out_5(out_3[5]));
  Comparator1bit comparator1bit_4 (
    .in_3(in_1[4]), .in_4(in_2[4]), .in_1(comparator1bit_3_out_6), .in_2(comparator1bit_3_out_7),
    .out_6(comparator1bit_4_out_6), .out_7(comparator1bit_4_out_7), .out_5(out_3[4]));
  Comparator1bit comparator1bit_5 (
    .in_3(in_1[3]), .in_4(in_2[3]), .in_1(comparator1bit_4_out_6), .in_2(comparator1bit_4_out_7),
    .out_6(comparator1bit_5_out_6), .out_7(comparator1bit_5_out_7), .out_5(out_3[3]));
  Comparator1bit comparator1bit_6 (
    .in_3(in_1[2]), .in_4(in_2[2]), .in_1(comparator1bit_5_out_6), .in_2(comparator1bit_5_out_7),
    .out_6(comparator1bit_6_out_6), .out_7(comparator1bit_6_out_7), .out_5(out_3[2]));
  Comparator1bit comparator1bit_7 (
    .in_3(in_1[1]), .in_4(in_2[1]), .in_1(comparator1bit_6_out_6), .in_2(comparator1bit_6_out_7),
    .out_6(comparator1bit_7_out_6), .out_7(comparator1bit_7_out_7), .out_5(out_3[1]));
  Comparator1bit comparator1bit_8 (
    .in_3(in_1[0]), .in_4(in_2[0]), .in_1(comparator1bit_7_out_6), .in_2(comparator1bit_7_out_7),
    .out_6(out_4), .out_7(out_5), .out_5(out_3[0]));
endmodule

module Comparator1bit (
  input  in_1,
  input  in_2,
  input  in_3,
  input  in_4,
  output out_5,
  output out_6,
  output out_7
);

  wire and_2_out, not_1_out;

  xor xor_1 (out_5, in_3, in_4);
  not not_1 (not_1_out, out_5);
  and and_1 (out_6, not_1_out, in_1);
  and and_2 (and_2_out, in_1, in_3, out_5);
  or or_1 (out_7, and_2_out, in_2);
endmodule

module ALU (
  input  [7:0] in_1,
  input  [7:0] in_2,
  input  in_3,
  input  in_4,
  input  in_5,
  input  in_6,
  output out_7,
  output out_8,
  output out_9,
  output [7:0] out_10,
  output out_11
);

  wire adder8bit_1_out_4, decoder8_1_out_4, decoder8_1_out_5, decoder8_1_out_6, decoder8_1_out_7,
       decoder8_1_out_8, decoder8_1_out_9, decoder8_1_out_10, decoder8_1_out_11, leftshifters_1_out_4,
       rightshifters_1_out_3;
  wire [7:0] adder8bit_1_out_5, ander_1_out_3, comparator8bit_1_out_3, leftshifters_1_out_3, notter_1_out_2,
       orer_1_out_3, rightshifters_1_out_4, xorer_1_out_3;

  XORer xorer_1 (.in_1(in_1), .in_2(in_2), .out_3(xorer_1_out_3));
  ORer orer_1 (.in_1(in_1), .in_2(in_2), .out_3(orer_1_out_3));
  ANDer ander_1 (.in_1(in_1), .in_2(in_2), .out_3(ander_1_out_3));
  NoTter notter_1 (.in_1(in_1), .out_2(notter_1_out_2));
  rightshifters rightshifters_1 (
    .in_1(in_1), .in_2(in_3), .out_3(rightshifters_1_out_3), .out_4(rightshifters_1_out_4));
  adder8bit adder8bit_1 (.in_2(in_3), .in_3(in_2), .in_1(in_1), .out_4(adder8bit_1_out_4), .out_5(adder8bit_1_out_5));
  Comparator8bit comparator8bit_1 (
    .in_1(in_1), .in_2(in_2), .out_4(out_7), .out_5(out_8), .out_3(comparator8bit_1_out_3));
  leftshifters leftshifters_1 (.in_2(in_1), .in_1(in_3), .out_4(leftshifters_1_out_4), .out_3(leftshifters_1_out_3));
  assign out_11 = decoder8_1_out_6 ? leftshifters_1_out_4 : 1'bz;  // Controlled_Buffer controlled_buffer_1
  assign out_11 = decoder8_1_out_5 ? rightshifters_1_out_3 : 1'bz;  // Controlled_Buffer controlled_buffer_2
  assign out_11 = decoder8_1_out_4 ? adder8bit_1_out_4 : 1'bz;  // Controlled_Buffer controlled_buffer_3
  enabler8bit enabler8bit_1 (.in_1(comparator8bit_1_out_3), .in_2(decoder8_1_out_11), .out_3(out_10));
  enabler8bit enabler8bit_2 (.in_1(xorer_1_out_3), .in_2(decoder8_1_out_10), .out_3(out_10));
  enabler8bit enabler8bit_3 (.in_1(orer_1_out_3), .in_2(decoder8_1_out_9), .out_3(out_10));
  enabler8bit enabler8bit_4 (.in_1(ander_1_out_3), .in_2(decoder8_1_out_8), .out_3(out_10));
  enabler8bit enabler8bit_5 (.in_1(notter_1_out_2), .in_2(decoder8_1_out_7), .out_3(out_10));
  enabler8bit enabler8bit_6 (.in_1(leftshifters_1_out_3), .in_2(decoder8_1_out_6), .out_3(out_10));
  enabler8bit enabler8bit_7 (.in_1(rightshifters_1_out_4), .in_2(decoder8_1_out_5), .out_3(out_10));
  enabler8bit enabler8bit_8 (.in_1(adder8bit_1_out_5), .in_2(decoder8_1_out_4), .out_3(out_10));
  decoder8 decoder8_1 (
    .in_3(in_6), .in_1(in_4), .in_2(in_5), .out_4(decoder8_1_out_4), .out_5(decoder8_1_out_5),
    .out_6(decoder8_1_out_6), .out_7(decoder8_1_out_7), .out_8(decoder8_1_out_8), .out_9(decoder8_1_out_9),
    .out_10(decoder8_1_out_10), .out_11(decoder8_1_out_11));
  Zero zero_1 (.in_1(out_10), .out_2(out_9));
endmodule

module decoder8 (
  input  in_1,
  input  in_2,
  input  in_3,
  output out_4,
  output out_5,
  output out_6,
  output out_7,
  output out_8,
  output out_9,
  output out_10,
  output out_11
);

  wire not_1_out, not_2_out, not_3_out;

  not not_1 (not_1_out, in_3);
  not not_2 (not_2_out, in_2);
  not not_3 (not_3_out, in_1);
  and and_1 (out_4, not_3_out, not_2_out, not_1_out);
  and and_2 (out_5, not_3_out, not_2_out, in_3);
  and and_3 (out_6, not_3_out, in_2, not_1_out);
  and and_4 (out_7, not_3_out, in_2, in_3);
  and and_5 (out_8, in_1, not_2_out, not_1_out);
  and and_6 (out_9, in_1, not_2_out, in_3);
  and and_7 (out_10, in_1, in_2, not_1_out);
  and and_8 (out_11, in_1, in_2, in_3);
endmodule

module enabler8bit (
  input  [7:0] in_1,
  input  in_2,
  output [7:0] out_3
);

  enabler enabler_1 (
    .in_1(in_1[0]), .in_2(in_1[1]), .in_3(in_1[2]), .in_4(in_1[3]), .in_5(in_1[4]), .in_6(in_1[5]),
    .in_7(in_1[6]), .in_8(in_1[7]), .in_9(in_2), .out_10(out_3[0]), .out_11(out_3[1]), .out_12(out_3[2]),
    .out_13(out_3[3]), .out_14(out_3[4]), .out_15(out_3[5]), .out_16(out_3[6]), .out_17(out_3[7]));
endmodule

module bus1 (
  input  [7:0] in_1,
  input  in_2,
  output [7:0] out_3
);

  wire not_1_out;

  not not_1 (not_1_out, in_2);
  or or_1 (out_3[0], in_1[0], in_2);
  and and_1 (out_3[1], in_1[1], not_1_out);
  and and_2 (out_3[2], in_1[2], not_1_out);
  and and_3 (out_3[3], in_1[3], not_1_out);
  and and_4 (out_3[4], in_1[4], not_1_out);
  and and_5 (out_3[5], in_1[5], not_1_out);
  and and_6 (out_3[6], in_1[6], not_1_out);
  and and_7 (out_3[7], in_1[7], not_1_out);
endmodule

module decoder16 (
  input  in_1,
  input  in_2,
  input  in_3,
  input  in_4,
  output out_5,
  output out_6,
  output out_7,
  output out_8,
  output out_9,
  output out_10,
  output out_11,
  output out_12,
  output out_13,
  output out_14,
  output out_15,
  output out_16,
  output out_17,
  output out_18,
  output out_19,
  output out_20
);

  wire decoder8_1_out_4, decoder8_1_out_5, decoder8_1_out_6, decoder8_1_out_7, decoder8_1_out_8,
       decoder8_1_out_9, decoder8_1_out_10, decoder8_1_out_11, decoder8_2_out_4, decoder8_2_out_5,
       decoder8_2_out_6, decoder8_2_out_7, decoder8_2_out_8, decoder8_2_out_9, decoder8_2_out_10,
       decoder8_2_out_11, not_1_out;

  decoder8 decoder8_1 (
    .in_3(in_4), .in_1(in_2), .in_2(in_3), .out_4(decoder8_1_out_4), .out_5(decoder8_1_out_5),
    .out_6(decoder8_1_out_6), .out_7(decoder8_1_out_7), .out_8(decoder8_1_out_8), .out_9(decoder8_1_out_9),
    .out_10(decoder8_1_out_10), .out_11(decoder8_1_out_11));
  decoder8 decoder8_2 (
    .in_3(in_4), .in_1(in_2), .in_2(in_3), .out_4(decoder8_2_out_4), .out_5(decoder8_2_out_5),
    .out_6(decoder8_2_out_6), .out_7(decoder8_2_out_7), .out_8(decoder8_2_out_8), .out_9(decoder8_2_out_9),
    .out_10(decoder8_2_out_10), .out_11(decoder8_2_out_11));
  not not_1 (not_1_out, in_1);
  and and_1 (out_5, decoder8_1_out_11, in_1);
  and and_2 (out_6, decoder8_1_out_10, in_1);
  and and_3 (out_7, decoder8_1_out_9, in_1);
  and and_4 (out_8, decoder8_1_out_8, in_1);
  and and_5 (out_9, decoder8_1_out_7, in_1);
  and and_6 (out_10, decoder8_1_out_6, in_1);
  and and_7 (out_11, decoder8_1_out_5, in_1);
  and and_8 (out_12, decoder8_1_out_4, in_1);
  and and_9 (out_13, decoder8_2_out_11, not_1_out);
  and and_10 (out_14, decoder8_2_out_10, not_1_out);
  and and_11 (out_15, decoder8_2_out_9, not_1_out);
  and and_12 (out_16, decoder8_2_out_8, not_1_out);
  and and_13 (out_17, decoder8_2_out_7, not_1_out);
  and and_14 (out_18, decoder8_2_out_6, not_1_out);
  and and_15 (out_19, decoder8_2_out_5, not_1_out);
  and and_16 (out_20, decoder8_2_out_4, not_1_out);
endmodule

module RAM256_4 (
  input  in_1,
  input  in_2,
  input  in_3,
  input  [7:0] in_4,
  input  in_5,
  input  in_6,
  input  in_7,
  output [7:0] out_8
);

  RAM256Cell ram256cell_1 (.in_1(in_3), .in_3(in_1), .in_4(in_6), .in_5(in_7), .in_2(in_4), .out_6(out_8));
  RAM256Cell ram256cell_2 (.in_1(in_5), .in_3(in_1), .in_4(in_6), .in_5(in_7), .in_2(in_4), .out_6(out_8));
  RAM256Cell ram256cell_3 (.in_1(in_3), .in_3(in_2), .in_4(in_6), .in_5(in_7), .in_2(in_4), .out_6(out_8));
  RAM256Cell ram256cell_4 (.in_1(in_5), .in_3(in_2), .in_4(in_6), .in_5(in_7), .in_2(in_4), .out_6(out_8));
endmodule

module RAM256_16 (
  input  in_1,
  input  in_2,
  input  in_3,
  input  in_4,
  input  in_5,
  input  [7:0] in_6,
  input  in_7,
  input  in_8,
  input  in_9,
  input  in_10,
  input  in_11,
  output [7:0] out_12
);

  RAM256_4 ram256_4_1 (
    .in_3(in_5), .in_5(in_7), .in_6(in_10), .in_1(in_1), .in_7(in_11), .in_2(in_2), .in_4(in_6),
    .out_8(out_12));
  RAM256_4 ram256_4_2 (
    .in_3(in_8), .in_5(in_9), .in_6(in_10), .in_1(in_1), .in_7(in_11), .in_2(in_2), .in_4(in_6),
    .out_8(out_12));
  RAM256_4 ram256_4_3 (
    .in_3(in_5), .in_5(in_7), .in_6(in_10), .in_1(in_3), .in_7(in_11), .in_2(in_4), .in_4(in_6),
    .out_8(out_12));
  RAM256_4 ram256_4_4 (
    .in_3(in_8), .in_5(in_9), .in_6(in_10), .in_1(in_3), .in_7(in_11), .in_2(in_4), .in_4(in_6),
    .out_8(out_12));
endmodule

module RAM256_64 (
  input  in_1,
  input  in_2,
  input  in_3,
  input  in_4,
  input  in_5,
  input  in_6,
  input  in_7,
  input  in_8,
  input  in_9,
  input  in_10,
  input  in_11,
  input  in_12,
  input  in_13,
  input  in_14,
  input  in_15,
  input  in_16,
  input  [7:0] in_17,
  input  in_18,
  input  in_19,
  output [7:0] out_20
);

  RAM256_16 ram256_16_1 (
    .in_5(in_9), .in_7(in_10), .in_8(in_11), .in_9(in_12), .in_10(in_18), .in_11(in_19), .in_1(in_1),
    .in_2(in_2), .in_3(in_3), .in_4(in_4), .in_6(in_17), .out_12(out_20));
  RAM256_16 ram256_16_2 (
    .in_5(in_13), .in_7(in_14), .in_8(in_15), .in_9(in_16), .in_10(in_18), .in_11(in_19), .in_1(in_1),
    .in_2(in_2), .in_3(in_3), .in_4(in_4), .in_6(in_17), .out_12(out_20));
  RAM256_16 ram256_16_3 (
    .in_5(in_9), .in_7(in_10), .in_8(in_11), .in_9(in_12), .in_10(in_18), .in_11(in_19), .in_1(in_5),
    .in_2(in_6), .in_3(in_7), .in_4(in_8), .in_6(in_17), .out_12(out_20));
  RAM256_16 ram256_16_4 (
    .in_5(in_13), .in_7(in_14), .in_8(in_15), .in_9(in_16), .in_10(in_18), .in_11(in_19), .in_1(in_5),
    .in_2(in_6), .in_3(in_7), .in_4(in_8), .in_6(in_17), .out_12(out_20));
endmodule

module RAM256 (
  input  [7:0] in_1,
  input  in_2,
  input  [7:0] in_3,
  input  in_4,
  input  in_5,
  output [7:0] out_6
);

  wire decoder16_1_out_5, decoder16_1_out_6, decoder16_1_out_7, decoder16_1_out_8, decoder16_1_out_9,
       decoder16_1_out_10, decoder16_1_out_11, decoder16_1_out_12, decoder16_1_out_13, decoder16_1_out_14,
       decoder16_1_out_15, decoder16_1_out_16, decoder16_1_out_17, decoder16_1_out_18, decoder16_1_out_19,
       decoder16_1_out_20, decoder16_2_out_5, decoder16_2_out_6, decoder16_2_out_7, decoder16_2_out_8,
       decoder16_2_out_9, decoder16_2_out_10, decoder16_2_out_11, decoder16_2_out_12, decoder16_2_out_13,
       decoder16_2_out_14, decoder16_2_out_15, decoder16_2_out_16, decoder16_2_out_17, decoder16_2_out_18,
       decoder16_2_out_19, decoder16_2_out_20, registerbe_1_out_11, registerbe_1_out_12, registerbe_1_out_13,
       registerbe_1_out_14, registerbe_1_out_15, registerbe_1_out_16, registerbe_1_out_17,
       registerbe_1_out_18;

  decoder16 decoder16_1 (
    .in_1(registerbe_1_out_15), .in_2(registerbe_1_out_16), .in_3(registerbe_1_out_17),
    .in_4(registerbe_1_out_18), .out_20(decoder16_1_out_20), .out_6(decoder16_1_out_6),
    .out_7(decoder16_1_out_7), .out_8(decoder16_1_out_8), .out_9(decoder16_1_out_9),
    .out_10(decoder16_1_out_10), .out_11(decoder16_1_out_11), .out_12(decoder16_1_out_12),
    .out_13(decoder16_1_out_13), .out_5(decoder16_1_out_5), .out_14(decoder16_1_out_14),
    .out_15(decoder16_1_out_15), .out_16(decoder16_1_out_16), .out_17(decoder16_1_out_17),
    .out_18(decoder16_1_out_18), .out_19(decoder16_1_out_19));
  registerBE registerbe_1 (
    .in_9(in_2), .in_10(1'b1), .in_1(in_1[0]), .in_2(in_1[1]), .in_3(in_1[2]), .in_4(in_1[3]),
    .in_5(in_1[4]), .in_6(in_1[5]), .in_7(in_1[6]), .in_8(in_1[7]), .out_11(registerbe_1_out_11),
    .out_12(registerbe_1_out_12), .out_13(registerbe_1_out_13), .out_14(registerbe_1_out_14),
    .out_15(registerbe_1_out_15), .out_16(registerbe_1_out_16), .out_17(registerbe_1_out_17),
    .out_18(registerbe_1_out_18));
  RAM256_64 ram256_64_1 (
    .in_9(decoder16_1_out_12), .in_10(decoder16_1_out_11), .in_11(decoder16_1_out_10),
    .in_12(decoder16_1_out_9), .in_13(decoder16_1_out_8), .in_14(decoder16_1_out_7),
    .in_15(decoder16_1_out_6), .in_16(decoder16_1_out_5), .in_1(decoder16_2_out_20), .in_18(in_4),
    .in_2(decoder16_2_out_19), .in_19(in_5), .in_3(decoder16_2_out_18), .in_4(decoder16_2_out_17),
    .in_5(decoder16_2_out_16), .in_6(decoder16_2_out_15), .in_7(decoder16_2_out_14), .in_17(in_3),
    .in_8(decoder16_2_out_13), .out_20(out_6));
  RAM256_64 ram256_64_2 (
    .in_9(decoder16_1_out_20), .in_10(decoder16_1_out_19), .in_11(decoder16_1_out_18),
    .in_12(decoder16_1_out_17), .in_13(decoder16_1_out_16), .in_14(decoder16_1_out_15),
    .in_15(decoder16_1_out_14), .in_16(decoder16_1_out_13), .in_1(decoder16_2_out_20), .in_18(in_4),
    .in_2(decoder16_2_out_19), .in_19(in_5), .in_3(decoder16_2_out_18), .in_4(decoder16_2_out_17),
    .in_5(decoder16_2_out_16), .in_6(decoder16_2_out_15), .in_7(decoder16_2_out_14), .in_17(in_3),
    .in_8(decoder16_2_out_13), .out_20(out_6));
  decoder16 decoder16_2 (
    .in_1(registerbe_1_out_11), .in_2(registerbe_1_out_12), .in_3(registerbe_1_out_13),
    .in_4(registerbe_1_out_14), .out_20(decoder16_2_out_20), .out_6(decoder16_2_out_6),
    .out_7(decoder16_2_out_7), .out_8(decoder16_2_out_8), .out_9(decoder16_2_out_9),
    .out_10(decoder16_2_out_10), .out_11(decoder16_2_out_11), .out_12(decoder16_2_out_12),
    .out_13(decoder16_2_out_13), .out_5(decoder16_2_out_5), .out_14(decoder16_2_out_14),
    .out_15(decoder16_2_out_15), .out_16(decoder16_2_out_16), .out_17(decoder16_2_out_17),
    .out_18(decoder16_2_out_18), .out_19(decoder16_2_out_19));
  RAM256_64 ram256_64_3 (
    .in_9(decoder16_1_out_12), .in_10(decoder16_1_out_11), .in_11(decoder16_1_out_10),
    .in_12(decoder16_1_out_9), .in_13(decoder16_1_out_8), .in_14(decoder16_1_out_7),
    .in_15(decoder16_1_out_6), .in_16(decoder16_1_out_5), .in_1(decoder16_2_out_12), .in_18(in_4),
    .in_2(decoder16_2_out_11), .in_19(in_5), .in_3(decoder16_2_out_10), .in_4(decoder16_2_out_9),
    .in_5(decoder16_2_out_8), .in_6(decoder16_2_out_7), .in_7(decoder16_2_out_6), .in_17(in_3),
    .in_8(decoder16_2_out_5), .out_20(out_6));
  RAM256_64 ram256_64_4 (
    .in_9(decoder16_1_out_20), .in_10(decoder16_1_out_19), .in_11(decoder16_1_out_18),
    .in_12(decoder16_1_out_17), .in_13(decoder16_1_out_16), .in_14(decoder16_1_out_15),
    .in_15(decoder16_1_out_14), .in_16(decoder16_1_out_13), .in_1(decoder16_2_out_12), .in_18(in_4),
    .in_2(decoder16_2_out_11), .in_19(in_5), .in_3(decoder16_2_out_10), .in_4(decoder16_2_out_9),
    .in_5(decoder16_2_out_8), .in_6(decoder16_2_out_7), .in_7(decoder16_2_out_6), .in_17(in_3),
    .in_8(decoder16_2_out_5), .out_20(out_6));
endmodule

module Clockes (
  output out_1,
  output out_2,
  output out_3,
  output out_4
);

  Clock #(.highDuration(2), .lowDuration(2)) clock_1 (.out(out_2));
  Clock #(.highDuration(2), .lowDuration(2), .phaseOffset(1)) clock_2 (.out(out_1));
  or or_1 (out_3, out_2, out_1);
  and and_1 (out_4, out_2, out_1);
endmodule

module stepper (
  input  in_1,
  input  in_2,
  output out_3,
  output out_4,
  output out_5,
  output out_6,
  output out_7,
  output out_8,
  output out_9,
  output out_10
);

  wire memorybit_1_out_3, memorybit_2_out_3, memorybit_3_out_3, memorybit_4_out_3, memorybit_5_out_3,
       memorybit_6_out_3, memorybit_7_out_3, memorybit_8_out_3, memorybit_9_out_3, memorybit_10_out_3,
       memorybit_11_out_3, memorybit_12_out_3, memorybit_13_out_3, not_1_out, not_2_out, not_3_out,
       not_4_out, not_5_out, not_6_out, not_7_out, not_8_out, not_9_out, or_1_out, or_3_out, or_4_out;

  or or_1 (or_1_out, in_1, out_10);
  not not_1 (not_1_out, or_1_out);
  not not_2 (not_2_out, in_2);
  or or_2 (out_3, or_1_out, not_3_out);
  not not_3 (not_3_out, memorybit_2_out_3);
  or or_3 (or_3_out, or_1_out, not_2_out);
  or or_4 (or_4_out, or_1_out, in_2);
  memorybit memorybit_1 (.in_2(or_3_out), .in_1(not_1_out), .out_3(memorybit_1_out_3));
  and and_1 (out_4, memorybit_2_out_3, not_4_out);
  not not_4 (not_4_out, memorybit_4_out_3);
  memorybit memorybit_2 (.in_2(or_4_out), .in_1(memorybit_1_out_3), .out_3(memorybit_2_out_3));
  memorybit memorybit_3 (.in_2(or_3_out), .in_1(memorybit_2_out_3), .out_3(memorybit_3_out_3));
  and and_2 (out_5, memorybit_4_out_3, not_5_out);
  memorybit memorybit_4 (.in_2(or_4_out), .in_1(memorybit_3_out_3), .out_3(memorybit_4_out_3));
  not not_5 (not_5_out, memorybit_6_out_3);
  memorybit memorybit_5 (.in_2(or_3_out), .in_1(memorybit_4_out_3), .out_3(memorybit_5_out_3));
  and and_3 (out_6, memorybit_6_out_3, not_6_out);
  memorybit memorybit_6 (.in_2(or_4_out), .in_1(memorybit_5_out_3), .out_3(memorybit_6_out_3));
  memorybit memorybit_7 (.in_2(or_3_out), .in_1(memorybit_6_out_3), .out_3(memorybit_7_out_3));
  not not_6 (not_6_out, memorybit_8_out_3);
  memorybit memorybit_8 (.in_2(or_4_out), .in_1(memorybit_7_out_3), .out_3(memorybit_8_out_3));
  and and_4 (out_7, memorybit_8_out_3, not_7_out);
  not not_7 (not_7_out, memorybit_10_out_3);
  memorybit memorybit_9 (.in_2(or_3_out), .in_1(memorybit_8_out_3), .out_3(memorybit_9_out_3));
  and and_5 (out_8, memorybit_10_out_3, not_8_out);
  memorybit memorybit_10 (.in_2(or_4_out), .in_1(memorybit_9_out_3), .out_3(memorybit_10_out_3));
  memorybit memorybit_11 (.in_2(or_3_out), .in_1(memorybit_10_out_3), .out_3(memorybit_11_out_3));
  not not_8 (not_8_out, memorybit_12_out_3);
  memorybit memorybit_12 (.in_2(or_4_out), .in_1(memorybit_11_out_3), .out_3(memorybit_12_out_3));
  and and_6 (out_9, memorybit_12_out_3, not_9_out);
  not not_9 (not_9_out, out_10);
  memorybit memorybit_13 (.in_2(or_3_out), .in_1(memorybit_12_out_3), .out_3(memorybit_13_out_3));
  memorybit memorybit_14 (.in_2(or_4_out), .in_1(memorybit_13_out_3), .out_3(out_10));
endmodule

module RAM16 (
  input  [7:0] in_1,
  input  in_2,
  input  [7:0] in_3,
  input  in_4,
  input  in_5,
  output [7:0] out_6
);

  wire [7:0] registerbesimple_1_out_4;

  registerBEsimple registerbesimple_1 (.in_1(in_1), .in_2(in_2), .in_3(1'b1), .out_4(registerbesimple_1_out_4));
  RAM256_4 ram256_4_1 (
    .in_3(registerbesimple_1_out_4[4]), .in_5(registerbesimple_1_out_4[5]), .in_6(in_4),
    .in_1(registerbesimple_1_out_4[0]), .in_7(in_5), .in_2(registerbesimple_1_out_4[1]), .in_4(in_3),
    .out_8(out_6));
  RAM256_4 ram256_4_2 (
    .in_3(registerbesimple_1_out_4[6]), .in_5(registerbesimple_1_out_4[7]), .in_6(in_4),
    .in_1(registerbesimple_1_out_4[0]), .in_7(in_5), .in_2(registerbesimple_1_out_4[1]), .in_4(in_3),
    .out_8(out_6));
  RAM256_4 ram256_4_3 (
    .in_3(registerbesimple_1_out_4[4]), .in_5(registerbesimple_1_out_4[5]), .in_6(in_4),
    .in_1(registerbesimple_1_out_4[2]), .in_7(in_5), .in_2(registerbesimple_1_out_4[3]), .in_4(in_3),
    .out_8(out_6));
  RAM256_4 ram256_4_4 (
    .in_3(registerbesimple_1_out_4[6]), .in_5(registerbesimple_1_out_4[7]), .in_6(in_4),
    .in_1(registerbesimple_1_out_4[2]), .in_7(in_5), .in_2(registerbesimple_1_out_4[3]), .in_4(in_3),
    .out_8(out_6));
endmodule

module P105 (
  input  in_1,
  input  in_2,
  input  in_3,
  input  in_4,
  input  in_5,
  input  [7:0] in_6,
  input  in_7,
  input  in_8,
  output [7:0] out_9
);

  wire ACC_out, ACCA_out, clockes_1_out_1, clockes_1_out_3, clockes_1_out_4, IAR_out, IARA_out, IR_out,
       MAR_out, or_1_out, or_2_out, R0_out, R0A_out, R1_out, R1A_out, R2_out, R2A_out, R3_out, R3A_out,
       RAM_out, RAMA_out, stepper_1_out_4, stepper_1_out_5, stepper_1_out_6, stepper_1_out_7,
       stepper_1_out_8, stepper_1_out_9, TMP_out, undriven, undriven_2, undriven_3, undriven_4, undriven_5,
       undriven_6, undriven_7, undriven_8, undriven_9, undriven_10, undriven_11, undriven_12, undriven_13,
       undriven_14, undriven_15, undriven_16, undriven_17;
  wire [7:0] bus1_1_out_3, registerbesimple_2_out_4, registerbesimple_9_out_4;

  and RAM (RAM_out, clockes_1_out_3, undriven);
  and ACC (ACC_out, clockes_1_out_3, undriven_2);
  and R0 (R0_out, clockes_1_out_3, undriven_3);
  and R1 (R1_out, clockes_1_out_3, undriven_4);
  and R2 (R2_out, clockes_1_out_3, undriven_5);
  and R3 (R3_out, clockes_1_out_3, undriven_6);
  and IAR (IAR_out, clockes_1_out_3, undriven_7);
  Clockes clockes_1 (.out_1(clockes_1_out_1), .out_3(clockes_1_out_3), .out_4(clockes_1_out_4));  // open: out_2
  registerBEsimple registerbesimple_1 (.in_1(out_9), .in_2(IARA_out), .in_3(IAR_out), .out_4(out_9));
  stepper stepper_1 (
    .in_2(clockes_1_out_1), .in_1(in_1), .out_8(stepper_1_out_8), .out_9(stepper_1_out_9),
    .out_4(stepper_1_out_4), .out_5(stepper_1_out_5), .out_6(stepper_1_out_6), .out_7(stepper_1_out_7));  // open: out_10, out_3
  registerBEsimple registerbesimple_2 (.in_1(out_9), .in_2(IR_out), .in_3(1'b1), .out_4(registerbesimple_2_out_4));
  RAM16 ram16_1 (.in_2(MAR_out), .in_4(RAMA_out), .in_5(RAM_out), .in_1(out_9), .in_3(out_9), .out_6(out_9));
  and MAR (MAR_out, clockes_1_out_4, undriven_8);
  and ACCA (ACCA_out, clockes_1_out_4, undriven_9);
  and RAMA (RAMA_out, clockes_1_out_4, undriven_10);
  and TMP (TMP_out, clockes_1_out_4, undriven_11);
  and R0A (R0A_out, clockes_1_out_4, undriven_12);
  and R1A (R1A_out, clockes_1_out_4, undriven_13);
  and R2A (R2A_out, clockes_1_out_4, undriven_14);
  and R3A (R3A_out, clockes_1_out_4, undriven_15);
  and IARA (IARA_out, clockes_1_out_4, undriven_16);
  and IR (IR_out, clockes_1_out_4, undriven_17);
  registerBEsimple registerbesimple_3 (.in_1(bus1_1_out_3), .in_2(ACCA_out), .in_3(ACC_out), .out_4(out_9));
  registerBEsimple registerbesimple_4 (.in_1(out_9), .in_2(or_1_out), .in_3(R0_out), .out_4(out_9));
  registerBEsimple registerbesimple_5 (.in_1(out_9), .in_2(or_2_out), .in_3(R1_out), .out_4(out_9));
  registerBEsimple registerbesimple_6 (.in_1(out_9), .in_2(R2A_out), .in_3(R2_out), .out_4(out_9));
  registerBEsimple registerbesimple_7 (.in_1(out_9), .in_2(R3A_out), .in_3(R3_out), .out_4(out_9));
  or or_1 (or_1_out, in_4, R0A_out);
  or or_2 (or_2_out, in_5, R1A_out);
  registerBEsimple registerbesimple_8 (.in_1(in_6), .in_2(in_7), .in_3(in_8), .out_4(out_9));
  registerBEsimple registerbesimple_9 (.in_1(out_9), .in_2(TMP_out), .in_3(1'b1), .out_4(registerbesimple_9_out_4));
  bus1 bus1_1 (.in_1(registerbesimple_9_out_4), .in_2(in_2), .out_3(bus1_1_out_3));
  // ALU alu_1: pin names not known; wires that end beside it: bus1_1_out_3, bus1_1_out_3, bus1_1_out_3

  // Notes on the sheet:
  //   IAR
  //   Enables
  //   IR
  //   Sets
  //   ACC
  //   R0
  //   R1
  //   R2
  //   R3
  //   TMP
endmodule

module P120 (
  input  in_1,
  input  in_2,
  input  in_3,
  input  in_4,
  input  in_5,
  input  in_6,
  input  in_7,
  output RegB,
  output TMP,
  output RegA,
  output ACC,
  output Flag,
  output ACC_2,
  output RegB_2,
  output _3,
  output ALU,
  output _1
);

  wire and_7_out, not_1_out;

  and and_1 (_3, in_2, in_4, in_7);
  and and_2 (ALU, in_2, in_4, in_6);
  and and_3 (_1, in_2, in_4, in_5);
  and and_4 (RegB, in_1, in_4);
  and and_5 (ACC, in_2, in_4);
  and and_6 (ACC_2, in_3, in_4, not_1_out);
  and and_7 (and_7_out, in_7, in_6, in_5);
  not not_1 (not_1_out, and_7_out);

  assign Flag = ACC;
  assign RegA = ACC;
  assign RegB_2 = ACC_2;
  assign TMP = RegB;

  // Notes on the sheet:
  //   2
  //   4
  //   Enables
  //   IR
  //   0
  //   5
  //   1
  //   2
  //   3
  //   6
  //   Sets
endmodule

module P119 (
  input  in_1,
  input  in_2,
  input  in_3,
  input  in_4,
  input  in_5,
  input  in_6,
  input  in_7,
  input  in_8,
  input  in_9,
  output _1,
  output _1_2,
  output _2,
  output _2_2,
  output _3,
  output _3_2,
  output _4,
  output _4_2
);

  wire and_1_out, and_2_out, and_3_out, and_4_out, and_5_out, and_6_out, and_7_out, and_8_out,
       decoder4_1_out_3, decoder4_1_out_4, decoder4_1_out_5, decoder4_1_out_6, decoder4_2_out_3,
       decoder4_2_out_4, decoder4_2_out_5, decoder4_2_out_6, decoder4_3_out_3, decoder4_3_out_4,
       decoder4_3_out_5, decoder4_3_out_6;

  or or_1 (_1, and_1_out, and_5_out);
  or or_2 (_2, and_2_out, and_6_out);
  or or_3 (_3, and_3_out, and_7_out);
  or or_4 (_4, and_4_out, and_8_out);
  and and_1 (and_1_out, decoder4_1_out_3, in_1, in_3);
  and and_2 (and_2_out, decoder4_1_out_4, in_1, in_3);
  and and_3 (and_3_out, decoder4_1_out_5, in_1, in_3);
  and and_4 (and_4_out, decoder4_1_out_6, in_1, in_3);
  and and_5 (and_5_out, decoder4_2_out_3, in_1, in_5);
  and and_6 (and_6_out, decoder4_2_out_4, in_1, in_5);
  and and_7 (and_7_out, decoder4_2_out_5, in_1, in_5);
  and and_8 (and_8_out, decoder4_2_out_6, in_1, in_5);
  decoder4 decoder4_1 (
    ._1(in_8), ._2(in_9), .out_3(decoder4_1_out_3), .out_4(decoder4_1_out_4), .out_5(decoder4_1_out_5),
    .out_6(decoder4_1_out_6));
  decoder4 decoder4_2 (
    ._1(in_6), ._2(in_7), .out_3(decoder4_2_out_3), .out_4(decoder4_2_out_4), .out_5(decoder4_2_out_5),
    .out_6(decoder4_2_out_6));
  decoder4 decoder4_3 (
    ._1(in_8), ._2(in_9), .out_3(decoder4_3_out_3), .out_4(decoder4_3_out_4), .out_5(decoder4_3_out_5),
    .out_6(decoder4_3_out_6));
  and and_9 (_1_2, decoder4_3_out_3, in_2, in_4);
  and and_10 (_2_2, decoder4_3_out_4, in_2, in_4);
  and and_11 (_3_2, decoder4_3_out_5, in_2, in_4);
  and and_12 (_4_2, decoder4_3_out_6, in_2, in_4);
endmodule

module decoder4 (
  input  _1,
  input  _2,
  output out_3,
  output out_4,
  output out_5,
  output out_6
);

  wire not_1_out, not_2_out;

  not not_1 (not_1_out, _1);
  not not_2 (not_2_out, _2);
  and and_1 (out_3, not_1_out, not_2_out);
  and and_2 (out_4, not_1_out, _2);
  and and_3 (out_5, _1, not_2_out);
  and and_4 (out_6, _1, _2);

  // Notes on the sheet:
  //   1
  //   2
  //   3
  //   4
endmodule

module loadandstoreP124 (
  input  in_1,
  input  in_2,
  input  in_3,
  input  in_4,
  output out_5,
  output out_6,
  output out_7,
  output out_8,
  output out_9,
  output out_10,
  output out_11,
  output out_12
);

  and and_1 (out_5, in_1, in_3);
  and and_2 (out_9, in_1, in_4);
  and and_3 (out_7, in_2, in_3);
  and and_4 (out_11, in_2, in_4);

  assign out_6 = out_5;
  assign out_8 = out_7;
  assign out_10 = out_9;
  assign out_12 = out_11;
endmodule

module DATAP127 (
  input  in_1,
  input  in_2,
  input  in_3,
  input  in_4,
  output out_5,
  output out_6,
  output out_7,
  output out_8,
  output out_9,
  output out_10,
  output out_11,
  output out_12
);

  and and_1 (out_5, in_1, in_4);
  and and_2 (out_9, in_2, in_4);
  and and_3 (out_11, in_3, in_4);

  assign out_6 = out_5;
  assign out_7 = out_5;
  assign out_8 = out_5;
  assign out_10 = out_9;
  assign out_12 = out_11;
endmodule

module JMPR_RB (
  input  in_1,
  input  in_2,
  output out_3,
  output out_4
);

  and and_1 (out_3, in_1, in_2);

  assign out_4 = out_3;
endmodule

module P112 (
  input  _2,
  input  _3,
  input  in_3,
  input  clke,
  input  clks,
  output bus1,
  output IR,
  output IAR,
  output MAR,
  output RAM,
  output IAR_2,
  output ACC,
  output ACC_2
);

  and and_1 (IAR, clke, _2);
  and and_2 (RAM, clke, _3);
  and and_3 (ACC, clke, in_3);
  and and_4 (IR, clks, _3);
  and and_5 (MAR, clks, _2);
  and and_6 (IAR_2, clks, in_3);
  and and_7 (ACC_2, clks, _2);

  assign bus1 = _2;

  // Notes on the sheet:
  //   Enable
  //   1
  //   Set
endmodule

module JMP (
  input  in_1,
  input  in_2,
  input  in_3,
  output out_4,
  output out_5,
  output out_6,
  output out_7
);

  and and_1 (out_4, in_1, in_3);
  and and_2 (out_6, in_2, in_3);

  assign out_5 = out_4;
  assign out_7 = out_6;
endmodule

module Flags (
  input  in_1,
  input  in_2,
  input  in_3,
  input  in_4,
  input  in_5,
  input  in_6,
  output out_7,
  output out_8,
  output out_9,
  output out_10
);

  wire and_1_out, and_2_out, and_3_out, and_4_out, not_1_out, or_1_out;

  not not_1 (not_1_out, in_1);
  and and_1 (and_1_out, not_1_out, in_2);
  and and_2 (and_2_out, not_1_out, in_3);
  and and_3 (and_3_out, not_1_out, in_4);
  and and_4 (and_4_out, not_1_out, in_5);
  registerBE registerbe_1 (
    .in_9(or_1_out), .in_10(1'b1), .in_1(and_1_out), .in_2(and_2_out), .in_3(and_3_out), .in_4(and_4_out),
    .out_11(out_7), .out_12(out_8), .out_13(out_9), .out_14(out_10));  // open: in_5, in_6, in_7, in_8, out_15, out_16, out_17, out_18
  or or_1 (or_1_out, in_1, in_6);
endmodule

module P134 (
  input  in_1,
  input  in_2,
  input  in_3,
  input  in_4,
  input  carryout,
  input  alarger,
  input  equal,
  input  zero,
  input  in_9,
  input  in_10,
  input  in_11,
  input  in_12,
  output out_13,
  output out_14,
  output out_15,
  output out_16,
  output out_17,
  output out_18,
  output out_19,
  output out_20
);

  wire and_4_out, and_5_out, and_6_out, and_7_out, or_1_out;

  and and_1 (out_13, in_1, in_4);
  and and_2 (out_17, in_2, in_4);
  and and_3 (out_19, in_3, or_1_out, in_4);
  and and_4 (and_4_out, carryout, in_9);
  and and_5 (and_5_out, alarger, in_10);
  and and_6 (and_6_out, equal, in_11);
  and and_7 (and_7_out, zero, in_12);
  or or_1 (or_1_out, and_4_out, and_5_out, and_6_out, and_7_out);

  assign out_14 = out_13;
  assign out_15 = out_13;
  assign out_16 = out_13;
  assign out_18 = out_17;
  assign out_20 = out_19;
endmodule

module Clearflag (
  input  in_1,
  input  in_2,
  output out_3,
  output out_4
);

  and and_1 (out_3, in_1, in_2);

  assign out_4 = out_3;
endmodule

module Enables (
  input  in_1,
  input  in_2,
  input  in_3,
  input  in_4,
  input  in_5,
  input  in_6,
  output out_7,
  output out_8,
  output out_9,
  output out_10,
  output out_11
);

  and and_1 (out_8, in_1, in_3);
  and and_2 (out_9, in_1, in_4);
  and and_3 (out_10, in_1, in_5);
  and and_4 (out_11, in_1, in_6);

  assign out_7 = in_2;
endmodule

module Sets (
  input  in_1,
  input  in_2,
  input  in_3,
  input  in_4,
  input  in_5,
  input  in_6,
  input  in_7,
  input  in_8,
  input  in_9,
  output out_10,
  output out_11,
  output out_12,
  output out_13,
  output out_14,
  output out_15,
  output out_16,
  output out_17
);

  and and_1 (out_10, in_1, in_2);
  and and_2 (out_11, in_1, in_3);
  and and_3 (out_12, in_1, in_4);
  and and_4 (out_13, in_1, in_5);
  and and_5 (out_14, in_1, in_6);
  and and_6 (out_15, in_1, in_7);
  and and_7 (out_16, in_1, in_8);
  and and_8 (out_17, in_1, in_9);
endmodule

module IR (
  input  [7:0] in_1,
  input  in_2,
  output out_3,
  output out_4,
  output out_5,
  output out_6,
  output out_7,
  output out_8,
  output out_9,
  output out_10
);

  registerBEsimple registerbesimple_1 (
    .in_1(in_1), .in_2(in_2), .in_3(1'b1), .out_4({out_3, out_4, out_5, out_6, out_7, out_8, out_9, out_10}));

  // Notes on the sheet:
  //   IR
endmodule

module Control (
  input  in_1,
  input  [7:0] in_2
);

  wire alu_1_p1, and_1_out, and_2_out, and_3_out, clockes_1_out_1, clockes_1_out_4, datap127_1_out_5,
       datap127_1_out_7, datap127_1_out_9, decoder8_1_out_4, decoder8_1_out_5, decoder8_1_out_6,
       decoder8_1_out_7, decoder8_1_out_8, decoder8_1_out_9, decoder8_1_out_10, decoder8_1_out_11,
       enables_1_p1, enables_1_p2, enables_1_p3, enables_1_p4, enables_1_p5, enables_1_p6, enables_1_p7,
       enables_1_p8, enables_1_p9, ir_1_out_3, ir_1_out_4, ir_1_out_5, ir_1_out_6, ir_1_out_7, ir_1_out_8,
       ir_1_out_9, ir_1_out_10, loadandstorep124_1_out_5, loadandstorep124_1_out_6, loadandstorep124_1_out_7,
       loadandstorep124_1_out_8, loadandstorep124_1_out_9, loadandstorep124_1_out_10,
       loadandstorep124_1_out_11, loadandstorep124_1_out_12, not_1_out, or_7_out, or_8_out, or_9_out,
       or_10_out, or_11_out, p112_1_acc, p112_1_acc_2, p112_1_bus1, p112_1_iar, p112_1_iar_2, p112_1_ir,
       p112_1_mar, p112_1_ram, p120_1__1, p120_1__3, p120_1_acc, p120_1_acc_2, p120_1_flag, p120_1_rega,
       p120_1_regb, p120_1_tmp, sets_1_out_10, sets_1_out_17, stepper_1_out_4, stepper_1_out_5,
       stepper_1_out_6, stepper_1_out_7, stepper_1_out_8, stepper_1_out_9, undriven, undriven_2;

  // Enables enables_1: pin names not known; wires that end beside it: enables_1_p1, enables_1_p2, enables_1_p3, enables_1_p4, enables_1_p5, enables_1_p6, enables_1_p7, enables_1_p8, enables_1_p9
  or or_1 (enables_1_p4, p112_1_bus1, datap127_1_out_5);
  or or_2 (enables_1_p5, p112_1_iar, datap127_1_out_7);
  or or_3 (enables_1_p6, p112_1_ram, loadandstorep124_1_out_7, undriven, undriven_2, datap127_1_out_9);
  or or_4 (enables_1_p7, p112_1_acc, p120_1_acc_2);
  or or_5 (enables_1_p8, p120_1_regb, loadandstorep124_1_out_11);
  or or_6 (enables_1_p9, p120_1_rega, loadandstorep124_1_out_5, loadandstorep124_1_out_9);
  // ALU alu_1: pin names not known; wires that end beside it: alu_1_p1, alu_1_p1
  Clockes clockes_1 (.out_1(clockes_1_out_1), .out_3(enables_1_p3), .out_4(clockes_1_out_4));  // open: out_2
  decoder8P124 decoder8p124_1 ();  // open: in_2, in_3, in_4, in_1, out_12, out_5, out_6, out_7, out_8, out_9, out_10, out_11
  stepper stepper_1 (
    .in_2(clockes_1_out_1), .in_1(in_1), .out_8(stepper_1_out_8), .out_9(stepper_1_out_9),
    .out_4(stepper_1_out_4), .out_5(stepper_1_out_5), .out_6(stepper_1_out_6), .out_7(stepper_1_out_7));  // open: out_10, out_3
  P112 p112_1 (
    .clke(enables_1_p3), ._2(stepper_1_out_4), ._3(stepper_1_out_5), .in_3(stepper_1_out_6),
    .clks(clockes_1_out_4), .bus1(p112_1_bus1), .IAR(p112_1_iar), .RAM(p112_1_ram), .ACC(p112_1_acc),
    .IR(p112_1_ir), .MAR(p112_1_mar), .IAR_2(p112_1_iar_2), .ACC_2(p112_1_acc_2));
  P119 p119_1 (
    .in_1(enables_1_p3), .in_3(enables_1_p1), .in_5(enables_1_p2), .in_6(ir_1_out_7), .in_7(ir_1_out_8),
    .in_8(ir_1_out_9), .in_9(ir_1_out_10), .in_2(clockes_1_out_4), .in_4(sets_1_out_17));  // open: _1_2, _2_2, _3_2, _4_2, _1, _2, _3, _4
  P120 p120_1 (
    .in_1(stepper_1_out_7), .in_4(ir_1_out_3), .in_5(ir_1_out_4), .in_6(ir_1_out_5), .in_2(stepper_1_out_8),
    .in_7(ir_1_out_6), .in_3(stepper_1_out_9), ._3(p120_1__3), .ALU(alu_1_p1), ._1(p120_1__1),
    .RegB(p120_1_regb), .RegA(p120_1_rega), .ACC_2(p120_1_acc_2), .TMP(p120_1_tmp), .ACC(p120_1_acc),
    .Flag(p120_1_flag));  // open: RegB_2
  IR ir_1 (
    .in_1(in_2), .in_2(sets_1_out_10), .out_3(ir_1_out_3), .out_4(ir_1_out_4), .out_5(ir_1_out_5),
    .out_6(ir_1_out_6), .out_7(ir_1_out_7), .out_8(ir_1_out_8), .out_9(ir_1_out_9), .out_10(ir_1_out_10));
  buf or_7 (or_7_out, p112_1_mar);  // OR_Gate
  or or_8 (or_8_out, p112_1_iar_2, loadandstorep124_1_out_6, loadandstorep124_1_out_10);
  or or_9 (or_9_out, p112_1_acc_2, p120_1_acc);
  // OR_Gate or_10 has open pins: out=or_10_out
  or or_11 (or_11_out, p120_1_flag, loadandstorep124_1_out_8);
  Sets sets_1 (
    .in_2(p112_1_ir), .in_3(or_7_out), .in_4(or_8_out), .in_5(or_9_out), .in_6(loadandstorep124_1_out_12),
    .in_7(p120_1_tmp), .in_8(or_10_out), .in_9(or_11_out), .in_1(clockes_1_out_4), .out_10(sets_1_out_10),
    .out_17(sets_1_out_17));  // open: out_11, out_12, out_13, out_14, out_15, out_16
  not not_1 (not_1_out, ir_1_out_3);
  decoder8 decoder8_1 (
    .in_3(ir_1_out_6), .in_1(ir_1_out_4), .in_2(ir_1_out_5), .out_4(decoder8_1_out_4),
    .out_5(decoder8_1_out_5), .out_6(decoder8_1_out_6), .out_7(decoder8_1_out_7), .out_8(decoder8_1_out_8),
    .out_9(decoder8_1_out_9), .out_10(decoder8_1_out_10), .out_11(decoder8_1_out_11));
  loadandstoreP124 loadandstorep124_1 (
    .in_3(and_1_out), .in_4(and_2_out), .in_1(stepper_1_out_7), .in_2(stepper_1_out_8),
    .out_5(loadandstorep124_1_out_5), .out_7(loadandstorep124_1_out_7), .out_9(loadandstorep124_1_out_9),
    .out_11(loadandstorep124_1_out_11), .out_6(loadandstorep124_1_out_6), .out_8(loadandstorep124_1_out_8),
    .out_10(loadandstorep124_1_out_10), .out_12(loadandstorep124_1_out_12));
  and and_1 (and_1_out, decoder8_1_out_4, not_1_out);
  and and_2 (and_2_out, decoder8_1_out_5, not_1_out);
  and and_3 (and_3_out, decoder8_1_out_6, not_1_out);
  // AND_Gate and_4 has open pins: in0=decoder8_1_out_7, in1=not_1_out, out=open
  // AND_Gate and_5 has open pins: in0=decoder8_1_out_8, in1=not_1_out, out=open
  // AND_Gate and_6 has open pins: in0=decoder8_1_out_9, in1=not_1_out, out=open
  // AND_Gate and_7 has open pins: in0=decoder8_1_out_10, in1=not_1_out, out=open
  // AND_Gate and_8 has open pins: in0=decoder8_1_out_11, in1=not_1_out, out=open
  DATAP127 datap127_1 (
    .in_4(and_3_out), .in_1(stepper_1_out_7), .in_2(stepper_1_out_8), .in_3(stepper_1_out_9),
    .out_5(datap127_1_out_5), .out_7(datap127_1_out_7), .out_9(datap127_1_out_9));  // open: out_11, out_6, out_8, out_10, out_12
endmodule

module decoder8P124 (
  input  in_1,
  input  in_2,
  input  in_3,
  input  in_4,
  output out_5,
  output out_6,
  output out_7,
  output out_8,
  output out_9,
  output out_10,
  output out_11,
  output out_12
);

  wire decoder8_1_out_4, decoder8_1_out_5, decoder8_1_out_6, decoder8_1_out_7, decoder8_1_out_8,
       decoder8_1_out_9, decoder8_1_out_10, decoder8_1_out_11, not_1_out;

  not not_1 (not_1_out, in_1);
  decoder8 decoder8_1 (
    .in_3(in_4), .in_1(in_2), .in_2(in_3), .out_4(decoder8_1_out_4), .out_5(decoder8_1_out_5),
    .out_6(decoder8_1_out_6), .out_7(decoder8_1_out_7), .out_8(decoder8_1_out_8), .out_9(decoder8_1_out_9),
    .out_10(decoder8_1_out_10), .out_11(decoder8_1_out_11));
  and and_1 (out_5, decoder8_1_out_4, not_1_out);
  and and_2 (out_6, decoder8_1_out_5, not_1_out);
  and and_3 (out_7, decoder8_1_out_6, not_1_out);
  and and_4 (out_8, decoder8_1_out_7, not_1_out);
  and and_5 (out_9, decoder8_1_out_8, not_1_out);
  and and_6 (out_10, decoder8_1_out_9, not_1_out);
  and and_7 (out_11, decoder8_1_out_10, not_1_out);
  and and_8 (out_12, decoder8_1_out_11, not_1_out);
endmodule

module Controlunit1 (
  input  clke,
  input  clks,
  input  s1,
  input  s2,
  input  s3,
  input  s4,
  input  s5,
  input  s6,
  input  IRs,
  input  RegB_s,
  input  RegB_e,
  input  carryout,
  input  RegA_e,
  input  alarger,
  input  equal,
  input  zero,
  input  [7:0] in_17,
  output bus1_1e,
  output IAR_1e,
  output RAM_1e,
  output MAR_1s,
  output bus1_2e,
  output IAR_1s,
  output IAR_2e,
  output bus1_3e,
  output ACC_1e,
  output ACC_1s,
  output RAM_3e,
  output IAR_3s,
  output RegB_3e,
  output MAR_5s,
  output IAR_4e,
  output ACC_3e,
  output MAR_6s,
  output RegA_2e,
  output IAR_4s,
  output ACC_4e,
  output ACC_4s,
  output RAM_2e,
  output RAM_5e,
  output IAR_5s,
  output RegA_3e,
  output IAR_6s,
  output RegB_2e,
  output Flags_2s,
  output IAR_3e,
  output MAR_4s,
  output bus1_4e,
  output RAM_4e,
  output MAR_2s,
  output ACC_3s,
  output R0_s,
  output RegB_2s,
  output RegB_3s,
  output R1_s,
  output MAR_3s,
  output IAR_2s,
  output R0_e,
  output R2_s,
  output RegB_4e,
  output RegB_4s,
  output RAM_1s,
  output R1_e,
  output R3_s,
  output R2_e,
  output IOclk_e,
  output IOclk_s,
  output R3_e,
  output TMP_1s,
  output ACC_2s,
  output RegB_1e,
  output Flags_1s,
  output IorO,
  output RegA_1e,
  output RegB_1s,
  output ACC_2e,
  output DorA,
  output ALU3,
  output ALU2,
  output ALU1
);

  wire decoder8p124_1_out_5, decoder8p124_1_out_6, decoder8p124_1_out_7, decoder8p124_1_out_8,
       decoder8p124_1_out_9, decoder8p124_1_out_10, decoder8p124_1_out_11, decoder8p124_1_out_12, ir_1_out_3,
       ir_1_out_4, ir_1_out_5, ir_1_out_6, ir_1_out_7, ir_1_out_8, ir_1_out_9, ir_1_out_10, or_1_out,
       p112_1_ir;

  IR ir_1 (
    .in_1(in_17), .in_2(or_1_out), .out_3(ir_1_out_3), .out_4(ir_1_out_4), .out_5(ir_1_out_5),
    .out_6(ir_1_out_6), .out_7(ir_1_out_7), .out_8(ir_1_out_8), .out_9(ir_1_out_9), .out_10(ir_1_out_10));
  P112 p112_1 (
    .clke(clke), ._2(s1), ._3(s2), .in_3(s3), .clks(clks), .bus1(bus1_1e), .IAR(IAR_1e), .RAM(RAM_1e),
    .ACC(ACC_1e), .IR(p112_1_ir), .MAR(MAR_1s), .IAR_2(IAR_1s), .ACC_2(ACC_1s));
  or or_1 (or_1_out, IRs, p112_1_ir);
  P119 p119_1 (
    .in_1(clke), .in_3(RegB_e), .in_5(RegA_e), .in_6(ir_1_out_7), .in_7(ir_1_out_8), .in_8(ir_1_out_9),
    .in_9(ir_1_out_10), .in_2(clks), .in_4(RegB_s), ._1_2(R0_s), ._2_2(R1_s), ._3_2(R2_s), ._4_2(R3_s),
    ._1(R0_e), ._2(R1_e), ._3(R2_e), ._4(R3_e));
  P120 p120_1 (
    .in_1(s4), .in_4(ir_1_out_3), .in_5(ir_1_out_4), .in_6(ir_1_out_5), .in_2(s5), .in_7(ir_1_out_6),
    .in_3(s6), ._3(ALU3), .ALU(ALU2), ._1(ALU1), .RegB(RegB_1e), .RegA(RegA_1e), .ACC_2(ACC_2e),
    .TMP(TMP_1s), .ACC(ACC_2s), .Flag(Flags_1s), .RegB_2(RegB_1s));
  decoder8P124 decoder8p124_1 (
    .in_2(ir_1_out_4), .in_3(ir_1_out_5), .in_4(ir_1_out_6), .in_1(ir_1_out_3),
    .out_12(decoder8p124_1_out_12), .out_5(decoder8p124_1_out_5), .out_6(decoder8p124_1_out_6),
    .out_7(decoder8p124_1_out_7), .out_8(decoder8p124_1_out_8), .out_9(decoder8p124_1_out_9),
    .out_10(decoder8p124_1_out_10), .out_11(decoder8p124_1_out_11));
  loadandstoreP124 loadandstorep124_1 (
    .in_3(decoder8p124_1_out_5), .in_4(decoder8p124_1_out_6), .in_1(s4), .in_2(s5), .out_5(RegA_2e),
    .out_7(RAM_2e), .out_9(RegA_3e), .out_11(RegB_2e), .out_6(MAR_2s), .out_8(RegB_2s), .out_10(MAR_3s),
    .out_12(RAM_1s));
  DATAP127 datap127_1 (
    .in_4(decoder8p124_1_out_7), .in_1(s4), .in_2(s5), .in_3(s6), .out_5(bus1_2e), .out_7(IAR_2e),
    .out_9(RAM_3e), .out_11(ACC_3e), .out_6(MAR_4s), .out_8(ACC_3s), .out_10(RegB_3s), .out_12(IAR_2s));
  JMPR_RB jmpr_rb_1 (.in_1(s4), .in_2(decoder8p124_1_out_8), .out_3(RegB_3e), .out_4(IAR_3s));
  JMP jmp_1 (
    .in_3(decoder8p124_1_out_9), .in_1(s4), .in_2(s5), .out_4(IAR_3e), .out_6(RAM_4e), .out_5(MAR_5s),
    .out_7(IAR_4s));
  P134 p134_1 (
    .carryout(carryout), .alarger(alarger), .equal(equal), .zero(zero), .in_4(decoder8p124_1_out_10),
    .in_1(s4), .in_2(s5), .in_9(ir_1_out_7), .in_10(ir_1_out_8), .in_11(ir_1_out_9), .in_12(ir_1_out_10),
    .in_3(s6), .out_15(IAR_4e), .out_17(ACC_4e), .out_19(RAM_5e), .out_13(bus1_3e), .out_16(ACC_4s),
    .out_18(IAR_5s), .out_20(IAR_6s), .out_14(MAR_6s));
  Clearflag clearflag_1 (.in_1(s4), .in_2(decoder8p124_1_out_11), .out_3(bus1_4e), .out_4(Flags_2s));
  P148 p148_1 (
    .D111(decoder8p124_1_out_12), .IR4(ir_1_out_7), .s4(s4), .IR5(ir_1_out_8), .s5(s5), .clks(clks),
    .clke(clke), .IOclks(IOclk_s), .IOclke(IOclk_e), .RegB_E(RegB_4e), .RegB_S(RegB_4s), .Inorout(IorO),
    .DorA(DorA));

  // Notes on the sheet:
  //   1
  //   2
  //   3
  //   4
  //   5
  //   6
endmodule

module P148 (
  input  s4,
  input  s5,
  input  clks,
  input  clke,
  input  D111,
  input  IR4,
  input  IR5,
  output RegB_E,
  output RegB_S,
  output IOclks,
  output IOclke,
  output Inorout,
  output DorA
);

  wire not_1_out;

  and and_1 (RegB_E, s4, D111, IR4);
  not not_1 (not_1_out, IR4);
  and and_2 (RegB_S, s5, D111, not_1_out);
  and and_3 (IOclks, clks, RegB_E);
  and and_4 (IOclke, clke, RegB_S);

  assign DorA = IR5;
  assign Inorout = IR4;
endmodule

module Controlunit2 (
  input  clke,
  input  clks,
  input  s1,
  input  s2,
  input  s3,
  input  s4,
  input  s5,
  input  s6,
  input  RegBe,
  input  RegAe,
  input  carryout,
  input  alarger,
  input  RegBs,
  input  equal,
  input  IRs,
  input  zero,
  input  [7:0] IRbus,
  output MAR_s,
  output bus1_e,
  output IAR_s,
  output IAR_e,
  output ACC_s,
  output RAM_e,
  output ACC_e,
  output RAM_s,
  output IO_e,
  output TMP_s,
  output RegB_e,
  output Flag_s,
  output R0_e,
  output R1_e,
  output RegA_e,
  output RegB_s,
  output R2_e,
  output R3_4,
  output IO_s,
  output ALU1,
  output R0_s,
  output ALU2,
  output R1_s,
  output ALU3,
  output R2_s,
  output R3_s,
  output out_44,
  output out_45
);

  wire controlunit1_1_acc_1e, controlunit1_1_acc_1s, controlunit1_1_acc_2e, controlunit1_1_acc_2s,
       controlunit1_1_acc_3e, controlunit1_1_acc_3s, controlunit1_1_acc_4e, controlunit1_1_acc_4s,
       controlunit1_1_bus1_1e, controlunit1_1_bus1_2e, controlunit1_1_bus1_3e, controlunit1_1_bus1_4e,
       controlunit1_1_flags_1s, controlunit1_1_flags_2s, controlunit1_1_iar_1e, controlunit1_1_iar_1s,
       controlunit1_1_iar_2e, controlunit1_1_iar_2s, controlunit1_1_iar_3e, controlunit1_1_iar_3s,
       controlunit1_1_iar_4e, controlunit1_1_iar_4s, controlunit1_1_iar_5s, controlunit1_1_iar_6s,
       controlunit1_1_mar_1s, controlunit1_1_mar_2s, controlunit1_1_mar_3s, controlunit1_1_mar_4s,
       controlunit1_1_mar_5s, controlunit1_1_mar_6s, controlunit1_1_ram_1e, controlunit1_1_ram_2e,
       controlunit1_1_ram_3e, controlunit1_1_ram_4e, controlunit1_1_ram_5e, controlunit1_1_rega_1e,
       controlunit1_1_rega_2e, controlunit1_1_rega_3e, controlunit1_1_regb_1e, controlunit1_1_regb_1s,
       controlunit1_1_regb_2e, controlunit1_1_regb_2s, controlunit1_1_regb_3e, controlunit1_1_regb_3s,
       controlunit1_1_regb_4e, controlunit1_1_regb_4s;

  or or_1 (bus1_e, controlunit1_1_bus1_1e, controlunit1_1_bus1_2e, controlunit1_1_bus1_3e, controlunit1_1_bus1_4e);
  or or_2 (IAR_e, controlunit1_1_iar_1e, controlunit1_1_iar_2e, controlunit1_1_iar_3e, controlunit1_1_iar_4e);
  or or_3 (RAM_e, controlunit1_1_ram_1e, controlunit1_1_ram_2e, controlunit1_1_ram_3e, controlunit1_1_ram_4e, controlunit1_1_ram_5e);
  or or_4 (ACC_e, controlunit1_1_acc_1e, controlunit1_1_acc_2e, controlunit1_1_acc_3e, controlunit1_1_acc_4e);
  or or_5 (RegB_e, controlunit1_1_regb_1e, controlunit1_1_regb_2e, controlunit1_1_regb_3e, controlunit1_1_regb_4e);
  or or_6 (RegA_e, controlunit1_1_rega_1e, controlunit1_1_rega_2e, controlunit1_1_rega_3e);
  Controlunit1 controlunit1_1 (
    .carryout(carryout), .alarger(alarger), .equal(equal), .zero(zero), .RegB_e(RegBe), .RegA_e(RegAe),
    .IRs(IRs), .in_17(IRbus), .clke(clke), .clks(clks), .s1(s1), .s2(s2), .RegB_s(RegBs), .s3(s3), .s4(s4),
    .s5(s5), .s6(s6), .MAR_2s(controlunit1_1_mar_2s), .RegB_2s(controlunit1_1_regb_2s),
    .MAR_3s(controlunit1_1_mar_3s), .RAM_1s(RAM_s), .bus1_2e(controlunit1_1_bus1_2e),
    .IAR_2e(controlunit1_1_iar_2e), .RAM_3e(controlunit1_1_ram_3e), .ACC_3e(controlunit1_1_acc_3e),
    .MAR_4s(controlunit1_1_mar_4s), .ACC_3s(controlunit1_1_acc_3s), .RegB_3s(controlunit1_1_regb_3s),
    .IAR_2s(controlunit1_1_iar_2s), .RegB_3e(controlunit1_1_regb_3e), .IAR_3s(controlunit1_1_iar_3s),
    .IAR_3e(controlunit1_1_iar_3e), .RAM_4e(controlunit1_1_ram_4e), .MAR_5s(controlunit1_1_mar_5s),
    .IAR_4s(controlunit1_1_iar_4s), .bus1_3e(controlunit1_1_bus1_3e), .IAR_4e(controlunit1_1_iar_4e),
    .ACC_4e(controlunit1_1_acc_4e), .RAM_5e(controlunit1_1_ram_5e), .R0_e(R0_e), .R1_e(R1_e), .R2_e(R2_e),
    .R3_e(R3_4), .RegB_1e(controlunit1_1_regb_1e), .RegA_1e(controlunit1_1_rega_1e),
    .ACC_2e(controlunit1_1_acc_2e), .ALU3(ALU3), .ALU2(ALU2), .ALU1(ALU1), .MAR_6s(controlunit1_1_mar_6s),
    .ACC_4s(controlunit1_1_acc_4s), .IAR_5s(controlunit1_1_iar_5s), .IAR_6s(controlunit1_1_iar_6s),
    .bus1_4e(controlunit1_1_bus1_4e), .Flags_2s(controlunit1_1_flags_2s), .RegB_4e(controlunit1_1_regb_4e),
    .IOclk_e(IO_e), .IorO(out_44), .DorA(out_45), .RegB_4s(controlunit1_1_regb_4s), .IOclk_s(IO_s),
    .IAR_1e(controlunit1_1_iar_1e), .RAM_1e(controlunit1_1_ram_1e), .ACC_1e(controlunit1_1_acc_1e),
    .bus1_1e(controlunit1_1_bus1_1e), .MAR_1s(controlunit1_1_mar_1s), .IAR_1s(controlunit1_1_iar_1s),
    .ACC_1s(controlunit1_1_acc_1s), .R0_s(R0_s), .R1_s(R1_s), .R2_s(R2_s), .R3_s(R3_s), .TMP_1s(TMP_s),
    .ACC_2s(controlunit1_1_acc_2s), .Flags_1s(controlunit1_1_flags_1s), .RegB_1s(controlunit1_1_regb_1s),
    .RegA_2e(controlunit1_1_rega_2e), .RAM_2e(controlunit1_1_ram_2e), .RegA_3e(controlunit1_1_rega_3e),
    .RegB_2e(controlunit1_1_regb_2e));
  or or_7 (MAR_s, controlunit1_1_mar_1s, controlunit1_1_mar_2s, controlunit1_1_mar_3s, controlunit1_1_mar_4s, controlunit1_1_mar_5s, controlunit1_1_mar_6s);
  or or_8 (IAR_s, controlunit1_1_iar_1s, controlunit1_1_iar_2s, controlunit1_1_iar_3s, controlunit1_1_iar_4s, controlunit1_1_iar_5s, controlunit1_1_iar_6s);
  or or_9 (ACC_s, controlunit1_1_acc_1s, controlunit1_1_acc_2s, controlunit1_1_acc_3s, controlunit1_1_acc_4s);
  or or_10 (Flag_s, controlunit1_1_flags_1s, controlunit1_1_flags_2s);
  or or_11 (RegB_s, controlunit1_1_regb_1s, controlunit1_1_regb_2s, controlunit1_1_regb_3s, controlunit1_1_regb_4s);
endmodule

module Controlunit3 (
  input  IRs,
  input  in_2,
  input  carryout,
  input  alarger,
  input  equal,
  input  zero,
  input  [7:0] in_7,
  input  R3_s,
  input  R2_s,
  input  R1_s,
  input  R0_s,
  input  [7:0] in_12,
  output MAR_s,
  output IAR_s,
  output ACC_s,
  output RAM_s,
  output TMP_s,
  output Flag_s,
  output IOclk_s,
  output bus1_e,
  output IAR_e,
  output RAM_e,
  output ACC_e,
  output IOclk_e,
  output ALU1,
  output ALU2,
  output DorA,
  output ALU3,
  output IorO,
  output [7:0] out_30
);

  wire clockes_1_out_1, clockes_1_out_3, clockes_1_out_4, controlunit2_1_acc_e, controlunit2_1_acc_s,
       controlunit2_1_bus1_e, controlunit2_1_flag_s, controlunit2_1_iar_e, controlunit2_1_iar_s,
       controlunit2_1_io_e, controlunit2_1_io_s, controlunit2_1_mar_s, controlunit2_1_r0_e,
       controlunit2_1_r0_s, controlunit2_1_r1_e, controlunit2_1_r1_s, controlunit2_1_r2_e,
       controlunit2_1_r2_s, controlunit2_1_r3_4, controlunit2_1_r3_s, controlunit2_1_ram_e,
       controlunit2_1_ram_s, controlunit2_1_rega_e, controlunit2_1_regb_e, controlunit2_1_regb_s,
       controlunit2_1_tmp_s, or_1_out, or_2_out, or_3_out, or_4_out, stepper_1_out_4, stepper_1_out_5,
       stepper_1_out_6, stepper_1_out_7, stepper_1_out_8, stepper_1_out_9;

  Enables enables_1 (
    .in_1(clockes_1_out_3), .in_2(controlunit2_1_bus1_e), .in_3(controlunit2_1_iar_e),
    .in_4(controlunit2_1_ram_e), .in_5(controlunit2_1_acc_e), .in_6(controlunit2_1_io_e), .out_7(bus1_e),
    .out_8(IAR_e), .out_9(RAM_e), .out_10(ACC_e), .out_11(IOclk_e));
  Clockes clockes_1 (.out_1(clockes_1_out_1), .out_3(clockes_1_out_3), .out_4(clockes_1_out_4));  // open: out_2
  stepper stepper_1 (
    .in_2(clockes_1_out_1), .in_1(in_2), .out_8(stepper_1_out_8), .out_9(stepper_1_out_9),
    .out_4(stepper_1_out_4), .out_5(stepper_1_out_5), .out_6(stepper_1_out_6), .out_7(stepper_1_out_7));  // open: out_10, out_3
  Controlunit2 controlunit2_1 (
    .RegBe(controlunit2_1_regb_e), .RegAe(controlunit2_1_rega_e), .carryout(carryout), .alarger(alarger),
    .equal(equal), .zero(zero), .IRbus(in_7), .clke(clockes_1_out_3), .clks(clockes_1_out_4),
    .s1(stepper_1_out_4), .s2(stepper_1_out_5), .s3(stepper_1_out_6), .s4(stepper_1_out_7),
    .s5(stepper_1_out_8), .s6(stepper_1_out_9), .RegBs(controlunit2_1_regb_s), .IRs(IRs),
    .R0_e(controlunit2_1_r0_e), .R1_e(controlunit2_1_r1_e), .R2_e(controlunit2_1_r2_e),
    .R3_4(controlunit2_1_r3_4), .ALU1(ALU1), .ALU2(ALU2), .ALU3(ALU3), .bus1_e(controlunit2_1_bus1_e),
    .IAR_e(controlunit2_1_iar_e), .RAM_e(controlunit2_1_ram_e), .ACC_e(controlunit2_1_acc_e),
    .IO_e(controlunit2_1_io_e), .RegB_e(controlunit2_1_regb_e), .RegA_e(controlunit2_1_rega_e),
    .out_44(IorO), .out_45(DorA), .MAR_s(controlunit2_1_mar_s), .IAR_s(controlunit2_1_iar_s),
    .ACC_s(controlunit2_1_acc_s), .RAM_s(controlunit2_1_ram_s), .TMP_s(controlunit2_1_tmp_s),
    .Flag_s(controlunit2_1_flag_s), .RegB_s(controlunit2_1_regb_s), .IO_s(controlunit2_1_io_s),
    .R0_s(controlunit2_1_r0_s), .R1_s(controlunit2_1_r1_s), .R2_s(controlunit2_1_r2_s),
    .R3_s(controlunit2_1_r3_s));
  R0123 r0123_1 (
    .in_2(or_1_out), .in_1(in_12), .in_3(controlunit2_1_r0_e), .in_4(or_2_out), .in_5(controlunit2_1_r1_e),
    .in_6(or_3_out), .in_7(controlunit2_1_r2_e), .in_8(or_4_out), .in_9(controlunit2_1_r3_4), .out_10(out_30));
  or or_1 (or_1_out, controlunit2_1_r0_s, R0_s);
  Sets sets_1 (
    .in_3(controlunit2_1_mar_s), .in_4(controlunit2_1_iar_s), .in_5(controlunit2_1_acc_s),
    .in_6(controlunit2_1_ram_s), .in_7(controlunit2_1_tmp_s), .in_8(controlunit2_1_flag_s),
    .in_9(controlunit2_1_io_s), .in_1(clockes_1_out_4), .out_11(MAR_s), .out_12(IAR_s), .out_13(ACC_s),
    .out_14(RAM_s), .out_15(TMP_s), .out_16(Flag_s), .out_17(IOclk_s));  // open: in_2, out_10
  or or_2 (or_2_out, controlunit2_1_r1_s, R1_s);
  or or_3 (or_3_out, controlunit2_1_r2_s, R2_s);
  or or_4 (or_4_out, controlunit2_1_r3_s, R3_s);
endmodule

module R0123 (
  input  [7:0] in_1,
  input  in_2,
  input  in_3,
  input  in_4,
  input  in_5,
  input  in_6,
  input  in_7,
  input  in_8,
  input  in_9,
  output [7:0] out_10
);

  registerBEsimple registerbesimple_1 (.in_1(in_1), .in_2(in_2), .in_3(in_3), .out_4(out_10));
  registerBEsimple registerbesimple_2 (.in_1(in_1), .in_2(in_4), .in_3(in_5), .out_4(out_10));
  registerBEsimple registerbesimple_3 (.in_1(in_1), .in_2(in_6), .in_3(in_7), .out_4(out_10));
  registerBEsimple registerbesimple_4 (.in_1(in_1), .in_2(in_8), .in_3(in_9), .out_4(out_10));
endmodule

module TMP (
  input  [7:0] in_1,
  input  in_2,
  output [7:0] out_3
);

  registerBEsimple registerbesimple_1 (.in_1(in_1), .in_2(in_2), .in_3(1'b1), .out_4(out_3));
endmodule

module ACC (
  input  [7:0] in_1,
  input  in_2,
  input  in_3,
  output [7:0] out_4
);

  registerBEsimple registerbesimple_1 (.in_1(in_1), .in_2(in_2), .in_3(in_3), .out_4(out_4));
endmodule

module IAR (
  input  [7:0] in_1,
  input  in_2,
  input  in_3,
  output [7:0] out_4
);

  registerBEsimple registerbesimple_1 (.in_1(in_1), .in_2(in_2), .in_3(in_3), .out_4(out_4));
endmodule
